# Fritzing sketch Main Circuit (saved by Fritzing 0.9.9b)
breadboards: 1

parts:
  Raspberry_Pi_1 = Raspberry Pi 3 [part_number=RPI-3-V1.2]
  ADC1 = MCP3008 [package=dil16]
  U1 = SLIDER [package=slider]
  U2 = SLIDER [package=slider]
  U3 = SLIDER [package=slider]
  U4 = SLIDER [package=slider]
  U5 = SLIDER [package=slider]
  U6 = SLIDER [package=slider]

nets:
  3.3V: Raspberry_Pi_1.3v3, ADC1.VREF, ADC1.VDD, U3.E, U5.E
  N1: Raspberry_Pi_1.GIPO10, ADC1.Din
  N2: Raspberry_Pi_1.GIPO9, ADC1.Dout
  N3: Raspberry_Pi_1.GIPO11, ADC1.CLK
  GND: Raspberry_Pi_1.GND, ADC1.DGND, ADC1.AGND, U1.A, U6.A
  N4: Raspberry_Pi_1.GIPO8, ADC1.CS/SHDN
  5V: Raspberry_Pi_1.5V
  N5: ADC1.CH2, U5.S
  N6: ADC1.CH3, U4.S
  N7: ADC1.CH4, U6.S
  N8: ADC1.CH5, U3.S
  N9: ADC1.CH6, U2.S
  N10: ADC1.CH7, U1.S

notes:
  Audio Thingy 1
  bass  |  mid  |  trebel
  EQ
  ________________________________________________
  distortion  |  reverb  |  compression
